// Logisim project J8.circ as structural Verilog: 1 circuit, main circuit main
module main (
  input  cin,
  input  A7,
  input  A6,
  input  A5,
  input  A4,
  input  A3,
  input  A2,
  input  A1,
  input  A0,
  input  B7,
  input  B6,
  input  B5,
  input  B4,
  input  B3,
  input  B2,
  input  B1,
  input  B0,
  input  [1:0] Operation_Code,
  output C0,
  output C1,
  output C2,
  output C3,
  output C4,
  output C5,
  output C6,
  output C7,
  output cout
);

  wire adder_1_cout, adder_1_out, adder_2_cout, adder_2_out, adder_3_cout, adder_3_out, adder_4_cout,
       adder_4_out, adder_5_cout, adder_5_out, adder_6_cout, adder_6_out, adder_7_cout, adder_7_out,
       adder_8_out, and_1_out, and_2_out, and_3_out, and_4_out, and_5_out, and_6_out, and_7_out, and_8_out,
       not_1_out, not_2_out, not_3_out, not_4_out, not_5_out, not_6_out, not_7_out, not_8_out, or_1_out,
       or_2_out, or_3_out, or_4_out, or_5_out, or_6_out, or_7_out, or_8_out;

  not not_1 (not_1_out, A0);
  and and_1 (and_1_out, A0, B0);
  or or_1 (or_1_out, A0, A0);
  Adder #(.width(1)) adder_1 (.a(A0), .b(B0), .out(adder_1_out), .cin(cin), .cout(adder_1_cout));
  not not_2 (not_2_out, A1);
  and and_2 (and_2_out, A1, B1);
  or or_2 (or_2_out, A1, B1);
  Adder #(.width(1)) adder_2 (.a(A1), .b(B1), .out(adder_2_out), .cin(adder_1_cout), .cout(adder_2_cout));
  not not_3 (not_3_out, A2);
  and and_3 (and_3_out, A2, B2);
  or or_3 (or_3_out, A2, B2);
  Adder #(.width(1)) adder_3 (.a(A2), .b(B2), .out(adder_3_out), .cin(adder_2_cout), .cout(adder_3_cout));
  not not_4 (not_4_out, A3);
  and and_4 (and_4_out, A3, B3);
  or or_4 (or_4_out, A3, B3);
  Adder #(.width(1)) adder_4 (.a(A3), .b(B3), .out(adder_4_out), .cin(adder_3_cout), .cout(adder_4_cout));
  not not_5 (not_5_out, A4);
  and and_5 (and_5_out, A4, B4);
  or or_5 (or_5_out, A4, B4);
  Adder #(.width(1)) adder_5 (.a(A4), .b(B4), .out(adder_5_out), .cin(adder_4_cout), .cout(adder_5_cout));
  not not_6 (not_6_out, A5);
  and and_6 (and_6_out, A5, B5);
  or or_6 (or_6_out, A5, B5);
  Adder #(.width(1)) adder_6 (.a(A5), .b(B5), .out(adder_6_out), .cin(adder_5_cout), .cout(adder_6_cout));
  not not_7 (not_7_out, A6);
  and and_7 (and_7_out, A6, B6);
  or or_7 (or_7_out, A6, B6);
  Adder #(.width(1)) adder_7 (.a(A6), .b(B6), .out(adder_7_out), .cin(adder_6_cout), .cout(adder_7_cout));
  not not_8 (not_8_out, A7);
  and and_8 (and_8_out, A7, B7);
  or or_8 (or_8_out, A7, B7);
  Adder #(.width(1)) adder_8 (.a(A7), .b(B7), .out(adder_8_out), .cin(adder_7_cout), .cout(cout));
  Multiplexer #(.select(2), .enable("false")) multiplexer_1 (
    .in0(not_7_out), .in1(and_7_out), .in2(or_7_out), .in3(adder_7_out), .out(C6), .sel(Operation_Code));
  Multiplexer #(.select(2), .enable("false")) multiplexer_2 (
    .in0(not_8_out), .in1(and_8_out), .in2(or_8_out), .in3(adder_8_out), .out(C7), .sel(Operation_Code));
  Multiplexer #(.select(2), .enable("false")) multiplexer_3 (
    .in0(not_5_out), .in1(and_5_out), .in2(or_5_out), .in3(adder_5_out), .out(C4), .sel(Operation_Code));
  Multiplexer #(.select(2), .enable("false")) multiplexer_4 (
    .in0(not_6_out), .in1(and_6_out), .in2(or_6_out), .in3(adder_6_out), .out(C5), .sel(Operation_Code));
  Multiplexer #(.select(2), .enable("false")) multiplexer_5 (
    .in0(not_3_out), .in1(and_3_out), .in2(or_3_out), .in3(adder_3_out), .out(C2), .sel(Operation_Code));
  Multiplexer #(.select(2), .enable("false")) multiplexer_6 (
    .in0(not_4_out), .in1(and_4_out), .in2(or_4_out), .in3(adder_4_out), .out(C3), .sel(Operation_Code));
  Multiplexer #(.select(2), .enable("false")) multiplexer_7 (
    .in0(not_2_out), .in1(and_2_out), .in2(or_2_out), .in3(adder_2_out), .out(C1), .sel(Operation_Code));
  Multiplexer #(.select(2), .enable("false")) multiplexer_8 (
    .in0(not_1_out), .in1(and_1_out), .in2(or_1_out), .in3(adder_1_out), .out(C0), .sel(Operation_Code));
endmodule
